# Fritzing sketch Great Pi Project (saved by Fritzing 0.9.3b)
breadboards: 1

parts:
  Red_Button = Pushbutton [package="[THT]"]
  Green_Button = Pushbutton [package="[THT]"]
  Blue_Button = Pushbutton [package="[THT]"]
  Voltage_Drop_Resistor = Resistor [tolerance=±5% resistance=1k package=THT]
  Raspberry_Pi_1 = Raspberry Pi 3 [part_number=RPI-3-V1.2]
  Flex_Resistor = Basic Flex Resistor
  RGB_LED = RGB LED - (4 legs) [package="5 mm [THT]"]
  Blue_Resistor_2 = Resistor [tolerance=±5% resistance=220 package=THT]
  Green_Resistor_2 = Resistor [tolerance=±5% resistance=220 package=THT]
  Red_Resistor = Resistor [tolerance=±5% resistance=220 package=THT]
  Green_Resistor_1 = Resistor [tolerance=±5% resistance=220 package=THT]
  Blue_Resistor_1 = Resistor [tolerance=±5% resistance=220 package=THT]

nets:
  N1: Red_Button.Pin_1, Red_Button.Pin_2, RGB_LED.red_cathode
  N2: Red_Button.Pin_3, Red_Button.Pin_4, Raspberry_Pi_1.GIPO22, Red_Resistor.Pin_1
  N3: Green_Button.Pin_1, Green_Button.Pin_2, RGB_LED.green_cathode
  N4: Green_Button.Pin_3, Green_Button.Pin_4, Raspberry_Pi_1.GIPO27, Green_Resistor_2.Pin_1
  N5: Blue_Button.Pin_1, Blue_Button.Pin_2, RGB_LED.blue_cathode
  N6: Blue_Button.Pin_3, Blue_Button.Pin_4, Raspberry_Pi_1.GIPO17, Blue_Resistor_2.Pin_1
  N7: Voltage_Drop_Resistor.Pin_0, Raspberry_Pi_1.GND, Red_Resistor.Pin_0, Green_Resistor_1.Pin_0, Blue_Resistor_1.Pin_0
  N8: Voltage_Drop_Resistor.Pin_1, Raspberry_Pi_1.GIPO18, Flex_Resistor.Pin_2
  N9: Raspberry_Pi_1.5V, Flex_Resistor.pin_1, RGB_LED.common_anode
  N10: Blue_Resistor_2.Pin_0, Blue_Resistor_1.Pin_1
  N11: Green_Resistor_2.Pin_0, Green_Resistor_1.Pin_1
